# Fritzing sketch Esquema PingPong (saved by Fritzing 0.9.0b)
breadboards: 1

parts:
  Parte1 = Arduino Uno (Rev3)
  U1 = POT [package=pot_alpha_rv16af-20]
  U2 = POT [package=pot_alpha_rv16af-20]

nets:
  N1: Parte1.A0, U2.S
  N2: Parte1.A1, U1.S
  N3: U1.A, U2.A
  N4: U1.E, U2.E
